// Logisim project lastname_firstname.circ as structural Verilog
module main (
);

  wire BEQ_Equal_bit, comparator_3_eq, comparator_4_eq, Is_JALR, STR, undriven_3, undriven_5;
  wire [3:0] Destination_reg_q, EX_OP, ID_OP, ID_Rx_Code, ID_Ry_Code, MEM_OP, register_2_q;
  wire [19:0] ID_Off;
  wire [23:0] bit_extender_1_out, bit_extender_3_out;
  wire [31:0] A, adder_1_out, adder_2_out, adder_4_out, and_1_out, B, BEQ_PC, bit_extender_2_out,
       dual_ported_register_file_1_out1, dual_ported_register_file_1_out2, EX_Off, EX_PC_q, EX_Result_q,
       ID_PC_q, multiplexer_1_out, multiplexer_2_out, not_1_out, PC_q, ram_1_data, register_5_q, rom_1_data,
       Shift_Result, undriven, undriven_2, undriven_4;

  Register #(.width(32)) PC (.D(multiplexer_1_out), .Q(PC_q));  // open: en, clk, clr
  Bit_Extender #(.in_width(32), .out_width(24)) bit_extender_1 (.in(PC_q), .out(bit_extender_1_out));
  Adder #(.width(32)) adder_1 (.a(32'h1), .b(PC_q), .out(adder_1_out));  // open: cin, cout
  Multiplexer #(.select(2), .width(32)) multiplexer_1 (
    .in0(adder_1_out), .in1(undriven), .in2(undriven_2), .out(multiplexer_1_out),
    .sel({BEQ_Equal_bit, Is_JALR}));  // open: in3, en
  ROM #(.addrWidth(24), .dataWidth(32)) rom_1 (.addr(bit_extender_1_out), .data(rom_1_data));  // open: sel
  Register #(.width(32)) Instruction_Reg (
    .D(rom_1_data), .en(1'b1), .Q({ID_OP, ID_Rx_Code, ID_Ry_Code, ID_Off}), .clk(undriven_3));  // open: clr
  Register #(.width(32)) ID_PC (.D(PC_q), .Q(ID_PC_q));  // open: en, clk, clr
  Dual_Ported_Register_File dual_ported_register_file_1 (
    .WrREGNO(ID_Rx_Code), .RdREGNO1(ID_Ry_Code), .RdREGNO2(ID_Off[3:0]), .INPUT(undriven_4),
    .OUT1(dual_ported_register_file_1_out1), .OUT2(dual_ported_register_file_1_out2));  // open: CLK, WrEN
  assign bit_extender_2_out = {{12{1'b0}}, ID_Off};  // Bit_Extender bit_extender_2
  Register #(.width(32)) register_1 (.D(bit_extender_2_out), .Q(EX_Off));  // open: en, clk, clr
  Register #(.width(4)) register_2 (.D(ID_Rx_Code), .Q(register_2_q));  // open: en, clk, clr
  Register #(.width(32)) Reg_A (.D(dual_ported_register_file_1_out1), .Q(B));  // open: en, clk, clr
  Register #(.width(32)) Reg_B (.D(dual_ported_register_file_1_out2), .Q(A));  // open: en, clk, clr
  Register #(.width(4)) u_EX_OP (.D(ID_OP), .Q(EX_OP));  // open: en, clk, clr
  Register #(.width(32)) EX_PC (.D(ID_PC_q), .Q(EX_PC_q));  // open: en, clk, clr
  Comparator #(.width(32)) comparator_1 (.a(A), .b(B), .eq(BEQ_Equal_bit));  // open: gt, lt
  Comparator #(.width(4)) comparator_2 (.a(EX_OP), .b(4'b0100), .eq(Is_JALR));  // open: gt, lt
  Adder #(.width(32)) adder_2 (.a(B), .b(A), .out(adder_2_out));  // open: cin, cout
  assign and_1_out = A & B;  // AND_Gate and_1, 32 bits wide
  Adder #(.width(32)) adder_3 (.a(EX_PC_q), .b(EX_Off), .out(BEQ_PC));  // open: cin, cout
  Adder #(.width(32)) adder_4 (.a(B), .b(EX_Off), .out(adder_4_out));  // open: cin, cout
  assign not_1_out = ~and_1_out;  // NOT_Gate not_1, 32 bits wide
  Multiplexer #(.select(2), .width(32)) multiplexer_2 (
    .in0(adder_2_out), .in1(adder_4_out), .in2(not_1_out), .in3(Shift_Result), .out(multiplexer_2_out),
    .en(undriven_5));  // open: sel
  Register #(.width(4)) Destination_reg (.D(register_2_q), .Q(Destination_reg_q));  // open: en, clk, clr
  Register #(.width(32)) EX_Result (.D(multiplexer_2_out), .Q(EX_Result_q));  // open: en, clk, clr
  Register #(.width(4)) register_3 (.D(EX_OP), .Q(MEM_OP));  // open: en, clk, clr
  assign bit_extender_3_out = {{20{1'b0}}, Destination_reg_q};  // Bit_Extender bit_extender_3
  Comparator #(.width(4)) comparator_3 (.a(MEM_OP), .b(4'b0101), .eq(comparator_3_eq));  // open: gt, lt
  RAM #(.addrWidth(24), .dataWidth(32), .bus("separate")) ram_1 (
    .addr(bit_extender_3_out), .din(EX_Result_q), .data(ram_1_data), .str(comparator_3_eq));  // open: sel, clk, ld, clr
  Register #(.width(24)) register_4 (.D(bit_extender_3_out));  // open: en, Q, clk, clr
  Register #(.width(32)) register_5 (.D(ram_1_data), .Q(register_5_q));  // open: en, clk, clr
  Register #(.width(4)) register_6 (.D(MEM_OP));  // open: en, Q, clk, clr
  Comparator #(.width(4)) comparator_4 (.a(MEM_OP), .b(4'b0110), .eq(comparator_4_eq));  // open: gt, lt
  Comparator #(.width(4)) comparator_5 (.a(MEM_OP), .b(4'b0111), .eq(STR));  // open: gt, lt

  // Other names for the same wires on the sheet: ID_Rz_Code[3:0] = ID_Off[3:0]
endmodule

module Dual_Ported_Register_File (
  input  CLK,
  input  WrEN,
  input  [3:0] WrREGNO,
  input  [3:0] RdREGNO1,
  input  [3:0] RdREGNO2,
  input  [31:0] INPUT,
  output [31:0] OUT1,
  output [31:0] OUT2
);

  wire En_a0, En_a1, En_a2, En_at, En_fp, En_k0, En_ra, En_s0, En_s1, En_s2, En_sp, En_t0, En_t1, En_t2,
       En_v0;
  wire [31:0] a0, a1, a2, at, fp, k0, ra, s0, s1, s2, sp, t0, t1, t2, v0, zero;

  Decoder #(.select(4), .disabled(0)) decoder_1 (
    .out1(En_at), .out2(En_v0), .out3(En_a0), .out4(En_a1), .out5(En_a2), .out6(En_t0), .out7(En_t1),
    .out8(En_t2), .out9(En_s0), .out10(En_s1), .out11(En_s2), .out12(En_k0), .out13(En_sp), .out14(En_fp),
    .out15(En_ra), .sel(WrREGNO), .en(WrEN));  // open: out0
  Register #(.width(32)) u_zero (.D(INPUT), .en(1'b0), .Q(zero), .clk(CLK));  // open: clr
  Register #(.width(32)) u_at (.D(INPUT), .en(En_at), .Q(at), .clk(CLK));  // open: clr
  Register #(.width(32)) u_v0 (.D(INPUT), .en(En_v0), .Q(v0), .clk(CLK));  // open: clr
  Register #(.width(32)) u_a0 (.D(INPUT), .en(En_a0), .Q(a0), .clk(CLK));  // open: clr
  Register #(.width(32)) u_a1 (.D(INPUT), .en(En_a1), .Q(a1), .clk(CLK));  // open: clr
  Register #(.width(32)) u_a2 (.D(INPUT), .en(En_a2), .Q(a2), .clk(CLK));  // open: clr
  Register #(.width(32)) u_t0 (.D(INPUT), .en(En_t0), .Q(t0), .clk(CLK));  // open: clr
  Register #(.width(32)) u_t1 (.D(INPUT), .en(En_t1), .Q(t1), .clk(CLK));  // open: clr
  Multiplexer #(.select(4), .width(32), .disabled(0), .enable("false")) multiplexer_1 (
    .in0(zero), .in1(at), .in2(v0), .in3(a0), .in4(a1), .in5(a2), .in6(t0), .in7(t1), .in8(t2), .in9(s0),
    .in10(s1), .in11(s2), .in12(k0), .in13(sp), .in14(fp), .in15(ra), .out(OUT2), .sel(RdREGNO2));
  Register #(.width(32)) u_t2 (.D(INPUT), .en(En_t2), .Q(t2), .clk(CLK));  // open: clr
  Register #(.width(32)) u_s0 (.D(INPUT), .en(En_s0), .Q(s0), .clk(CLK));  // open: clr
  Register #(.width(32)) u_s1 (.D(INPUT), .en(En_s1), .Q(s1), .clk(CLK));  // open: clr
  Register #(.width(32)) u_s2 (.D(INPUT), .en(En_s2), .Q(s2), .clk(CLK));  // open: clr
  Register #(.width(32)) u_k0 (.D(INPUT), .en(En_k0), .Q(k0), .clk(CLK));  // open: clr
  Register #(.width(32)) u_sp (.D(INPUT), .en(En_sp), .Q(sp), .clk(CLK));  // open: clr
  Register #(.width(32)) u_fp (.D(INPUT), .en(En_fp), .Q(fp), .clk(CLK));  // open: clr
  Register #(.width(32)) u_ra (.D(INPUT), .en(En_ra), .Q(ra), .clk(CLK));  // open: clr
  Multiplexer #(.select(4), .width(32), .disabled(0), .enable("false")) multiplexer_2 (
    .in0(zero), .in1(at), .in2(v0), .in3(a0), .in4(a1), .in5(a2), .in6(t0), .in7(t1), .in8(t2), .in9(s0),
    .in10(s1), .in11(s2), .in12(k0), .in13(sp), .in14(fp), .in15(ra), .out(OUT1), .sel(RdREGNO1));

  // Notes on the sheet:
  //   MODIFY AT YOUR OWN RISK
endmodule
